// Logisim project CPU.circ as structural Verilog: 5 circuits, main circuit GRF
module main (
  input  Reset,
  output [31:0] Instr,
  output RegWrite,
  output [4:0] RegAddr,
  output [31:0] RegData,
  output MemWrite,
  output [4:0] MemAddr,
  output [31:0] MemData
);

  wire alu_1_zero, ALUSrc, and_1_out, Branch, clock_1_out, Jump, MemtoReg, or_1_out, RegDst;
  wire [5:0] ALUControl;
  wire [15:0] bit_extender_1_out, bit_extender_4_out;
  wire [31:0] adder_1_out, adder_2_out, ALU_out, bit_extender_2_out, bit_extender_3_out, dm_1_rd,
       multiplexer_1_out, multiplexer_3_out, PC_q, RD1;

  // Probe on multiplexer_1_out
  Clock clock_1 (.out(clock_1_out));
  Register #(.width(32)) PC (.D(multiplexer_1_out), .Q(PC_q), .clk(clock_1_out), .clr(Reset));  // open: en
  Bit_Extender #(.in_width(32)) bit_extender_1 (.in(PC_q), .out(bit_extender_1_out));
  Multiplexer #(.width(32), .disabled(0), .enable("false")) multiplexer_1 (
    .in0(adder_1_out), .in1(adder_2_out), .out(multiplexer_1_out), .sel(or_1_out));
  Adder #(.width(32)) adder_1 (.a(PC_q), .b(32'h1), .out(adder_1_out));  // open: cin, cout
  or or_1 (or_1_out, Jump, and_1_out);
  ROM #(.addrWidth(16), .dataWidth(32)) rom_1 (.addr(bit_extender_1_out), .data(Instr));  // open: sel
  Controller controller_1 (
    .Jump(Jump), .Branch(Branch), .RegDst(RegDst), .RegWrite(RegWrite), .ALUControl(ALUControl),
    .ALUSrc(ALUSrc), .MemWrite(MemWrite), .MemtoReg(MemtoReg), .op(Instr[31:26]), .funct(Instr[5:0]));
  assign bit_extender_2_out = {{6{Instr[25]}}, Instr[25:0]};  // Bit_Extender bit_extender_2
  assign bit_extender_3_out = {{16{Instr[15]}}, Instr[15:0]};  // Bit_Extender bit_extender_3
  Multiplexer #(.width(5), .disabled(0), .enable("false")) multiplexer_2 (
    .in0(Instr[20:16]), .in1(Instr[15:11]), .out(RegAddr), .sel(RegDst));
  Multiplexer #(.width(32), .disabled(0), .enable("false")) multiplexer_3 (
    .in0(bit_extender_2_out), .in1(bit_extender_3_out), .out(multiplexer_3_out), .sel(and_1_out));
  and and_1 (and_1_out, alu_1_zero, Branch);
  Adder #(.width(32)) adder_2 (.a(multiplexer_3_out), .b(adder_1_out), .out(adder_2_out));  // open: cin, cout
  // Probe on RD1
  // Probe on MemData
  GRF grf_1 (
    .A1(Instr[25:21]), .A2(Instr[20:16]), .A3(RegAddr), .WD(RegData), .RD1(RD1), .RD2(MemData),
    .clk(clock_1_out), .reset(Reset), .WE(RegWrite));
  // Probe on {ALU_out[31:7], MemAddr, ALU_out[1:0]}
  ALU alu_1 (
    .op(ALUControl), .I1(RD1), .I2(MemData), .imm(Instr[15:0]), .ALU_choose(ALUSrc),
    .out({ALU_out[31:7], MemAddr, ALU_out[1:0]}), .zero(alu_1_zero));
  Bit_Extender #(.in_width(32)) bit_extender_4 (.in({ALU_out[31:7], MemAddr, ALU_out[1:0]}), .out(bit_extender_4_out));
  DM dm_1 (.clk(clock_1_out), .reset(Reset), .MemWrite(MemWrite), .A(bit_extender_4_out), .WD(MemData), .RD(dm_1_rd));
  // Probe on Instr
  // Probe on RegWrite
  // Probe on RegAddr
  // Probe on RegData
  // Probe on MemWrite
  // Probe on MemAddr
  // Probe on MemData
  Multiplexer #(.width(32), .disabled(0), .enable("false")) multiplexer_4 (
    .in0({ALU_out[31:7], MemAddr, ALU_out[1:0]}), .in1(dm_1_rd), .out(RegData), .sel(MemtoReg));

  // Other names for the same wires on the sheet: ALU_out[6:2] = MemAddr; funct[5:0] = Instr[5:0];
  //   imm[15:0] = Instr[15:0]; opcode[5:0] = Instr[31:26]; RD2[31:0] = MemData; WD[31:0] = RegData
endmodule

module GRF (
  input  clk,
  input  reset,
  input  WE,
  input  [4:0] A1,
  input  [4:0] A2,
  input  [4:0] A3,
  input  [31:0] WD,
  output [31:0] RD1,
  output [31:0] RD2
);

  wire WE0, WE1, WE2, WE3, WE4, WE5, WE6, WE7, WE8, WE9, WE10, WE11, WE12, WE13, WE14, WE15, WE16, WE17,
       WE18, WE19, WE20, WE21, WE22, WE23, WE24, WE25, WE26, WE27, WE28, WE29, WE30, WE31;
  wire [31:0] OUT1, OUT2, OUT3, OUT4, OUT5, OUT6, OUT7, OUT8, OUT9, OUT10, OUT11, OUT12, OUT13, OUT14, OUT15,
       OUT16, OUT17, OUT18, OUT19, OUT20, OUT21, OUT22, OUT23, OUT24, OUT25, OUT26, OUT27, OUT28, OUT29,
       OUT30, OUT31;

  Multiplexer #(.select(5), .width(32), .enable("false")) multiplexer_1 (
    .in0({32{1'b0}}), .in1(OUT1), .in2(OUT2), .in3(OUT3), .in4(OUT4), .in5(OUT5), .in6(OUT6), .in7(OUT7),
    .in8(OUT8), .in9(OUT9), .in10(OUT10), .in11(OUT11), .in12(OUT12), .in13(OUT13), .in14(OUT14),
    .in15(OUT15), .in16(OUT16), .in17(OUT17), .in18(OUT18), .in19(OUT19), .in20(OUT20), .in21(OUT21),
    .in22(OUT22), .in23(OUT23), .in24(OUT24), .in25(OUT25), .in26(OUT26), .in27(OUT27), .in28(OUT28),
    .in29(OUT29), .in30(OUT30), .in31(OUT31), .out(RD1), .sel(A1));
  Multiplexer #(.select(5), .width(32), .enable("false")) multiplexer_2 (
    .in0({32{1'b0}}), .in1(OUT1), .in2(OUT2), .in3(OUT3), .in4(OUT4), .in5(OUT5), .in6(OUT6), .in7(OUT7),
    .in8(OUT8), .in9(OUT9), .in10(OUT10), .in11(OUT11), .in12(OUT12), .in13(OUT13), .in14(OUT14),
    .in15(OUT15), .in16(OUT16), .in17(OUT17), .in18(OUT18), .in19(OUT19), .in20(OUT20), .in21(OUT21),
    .in22(OUT22), .in23(OUT23), .in24(OUT24), .in25(OUT25), .in26(OUT26), .in27(OUT27), .in28(OUT28),
    .in29(OUT29), .in30(OUT30), .in31(OUT31), .out(RD2), .sel(A2));
  Demultiplexer #(.select(5), .disabled(0), .enable("false")) demultiplexer_1 (
    .out0(WE0), .out1(WE1), .out2(WE2), .out3(WE3), .out4(WE4), .out5(WE5), .out6(WE6), .out7(WE7),
    .out8(WE8), .out9(WE9), .out10(WE10), .out11(WE11), .out12(WE12), .out13(WE13), .out14(WE14),
    .out15(WE15), .out16(WE16), .out17(WE17), .out18(WE18), .out19(WE19), .out20(WE20), .out21(WE21),
    .out22(WE22), .out23(WE23), .out24(WE24), .out25(WE25), .out26(WE26), .out27(WE27), .out28(WE28),
    .out29(WE29), .out30(WE30), .out31(WE31), .in(WE), .sel(A3));
  Register #(.width(32)) register_1 (.en(WE0), .clk(clk), .clr(reset));  // open: D, Q
  Register #(.width(32)) register_2 (.D(WD), .en(WE8), .Q(OUT8), .clk(clk), .clr(reset));
  Register #(.width(32)) register_3 (.D(WD), .en(WE16), .Q(OUT16), .clk(clk), .clr(reset));
  Register #(.width(32)) register_4 (.D(WD), .en(WE24), .Q(OUT24), .clk(clk), .clr(reset));
  Register #(.width(32)) register_5 (.D(WD), .en(WE1), .Q(OUT1), .clk(clk), .clr(reset));
  Register #(.width(32)) register_6 (.D(WD), .en(WE9), .Q(OUT9), .clk(clk), .clr(reset));
  Register #(.width(32)) register_7 (.D(WD), .en(WE17), .Q(OUT17), .clk(clk), .clr(reset));
  Register #(.width(32)) register_8 (.D(WD), .en(WE25), .Q(OUT25), .clk(clk), .clr(reset));
  Register #(.width(32)) register_9 (.D(WD), .en(WE2), .Q(OUT2), .clk(clk), .clr(reset));
  Register #(.width(32)) register_10 (.D(WD), .en(WE10), .Q(OUT10), .clk(clk), .clr(reset));
  Register #(.width(32)) register_11 (.D(WD), .en(WE18), .Q(OUT18), .clk(clk), .clr(reset));
  Register #(.width(32)) register_12 (.D(WD), .en(WE26), .Q(OUT26), .clk(clk), .clr(reset));
  Register #(.width(32)) register_13 (.D(WD), .en(WE3), .Q(OUT3), .clk(clk), .clr(reset));
  Register #(.width(32)) register_14 (.D(WD), .en(WE11), .Q(OUT11), .clk(clk), .clr(reset));
  Register #(.width(32)) register_15 (.D(WD), .en(WE19), .Q(OUT19), .clk(clk), .clr(reset));
  Register #(.width(32)) register_16 (.D(WD), .en(WE27), .Q(OUT27), .clk(clk), .clr(reset));
  Register #(.width(32)) register_17 (.D(WD), .en(WE4), .Q(OUT4), .clk(clk), .clr(reset));
  Register #(.width(32)) register_18 (.D(WD), .en(WE12), .Q(OUT12), .clk(clk), .clr(reset));
  Register #(.width(32)) register_19 (.D(WD), .en(WE20), .Q(OUT20), .clk(clk), .clr(reset));
  Register #(.width(32)) register_20 (.D(WD), .en(WE28), .Q(OUT28), .clk(clk), .clr(reset));
  Register #(.width(32)) register_21 (.D(WD), .en(WE5), .Q(OUT5), .clk(clk), .clr(reset));
  Register #(.width(32)) register_22 (.D(WD), .en(WE13), .Q(OUT13), .clk(clk), .clr(reset));
  Register #(.width(32)) register_23 (.D(WD), .en(WE21), .Q(OUT21), .clk(clk), .clr(reset));
  Register #(.width(32)) register_24 (.D(WD), .en(WE29), .Q(OUT29), .clk(clk), .clr(reset));
  Register #(.width(32)) register_25 (.D(WD), .en(WE6), .Q(OUT6), .clk(clk), .clr(reset));
  Register #(.width(32)) register_26 (.D(WD), .en(WE14), .Q(OUT14), .clk(clk), .clr(reset));
  Register #(.width(32)) register_27 (.D(WD), .en(WE22), .Q(OUT22), .clk(clk), .clr(reset));
  Register #(.width(32)) register_28 (.D(WD), .en(WE30), .Q(OUT30), .clk(clk), .clr(reset));
  Register #(.width(32)) register_29 (.D(WD), .en(WE7), .Q(OUT7), .clk(clk), .clr(reset));
  Register #(.width(32)) register_30 (.D(WD), .en(WE15), .Q(OUT15), .clk(clk), .clr(reset));
  Register #(.width(32)) register_31 (.D(WD), .en(WE23), .Q(OUT23), .clk(clk), .clr(reset));
  Register #(.width(32)) register_32 (.D(WD), .en(WE31), .Q(OUT31), .clk(clk), .clr(reset));
endmodule

module ALU (
  input  [5:0] op,
  input  [31:0] I1,
  input  [31:0] I2,
  input  [15:0] imm,
  input  ALU_choose,
  output [31:0] out,
  output zero
);

  wire comparator_1_eq;
  wire [31:0] add, addu, \and , bit_extender_1_out, bit_extender_2_out, bit_extender_3_out,
       bit_extender_4_out, bit_extender_5_out, bit_extender_6_out, bit_extender_7_out, bit_extender_8_out,
       multiplexer_1_out, multiplexer_2_out, multiplexer_3_out, multiplexer_4_out, multiplexer_5_out,
       multiplexer_6_out, multiplexer_7_out, multiplexer_8_out, multiplexer_9_out, multiplexer_11_out, \nor ,
       \or , sub, subu, \xor ;

  assign bit_extender_1_out = {{16{imm[15]}}, imm};  // Bit_Extender bit_extender_1
  assign bit_extender_2_out = {{16{imm[15]}}, imm};  // Bit_Extender bit_extender_2
  assign bit_extender_3_out = {{16{imm[15]}}, imm};  // Bit_Extender bit_extender_3
  assign bit_extender_4_out = {{16{imm[15]}}, imm};  // Bit_Extender bit_extender_4
  Multiplexer #(.width(32), .disabled(0), .enable("false")) multiplexer_1 (
    .in0(I2), .in1(bit_extender_1_out), .out(multiplexer_1_out), .sel(ALU_choose));
  Multiplexer #(.width(32), .disabled(0), .enable("false")) multiplexer_2 (
    .in0(I2), .in1(bit_extender_2_out), .out(multiplexer_2_out), .sel(ALU_choose));
  Multiplexer #(.width(32), .disabled(0), .enable("false")) multiplexer_3 (
    .in0(I2), .in1(bit_extender_3_out), .out(multiplexer_3_out), .sel(ALU_choose));
  Multiplexer #(.width(32), .disabled(0), .enable("false")) multiplexer_4 (
    .in0(I2), .in1(bit_extender_4_out), .out(multiplexer_4_out), .sel(ALU_choose));
  Adder #(.width(32)) adder_1 (.a(I1), .b(multiplexer_1_out), .out(add));  // open: cin, cout
  Adder #(.width(32)) adder_2 (.a(I1), .b(multiplexer_2_out), .out(addu));  // open: cin, cout
  Subtractor #(.width(32)) subtractor_1 (.a(I1), .b(multiplexer_3_out), .out(sub));  // open: bin, bout
  Subtractor #(.width(32)) subtractor_2 (.a(I1), .b(multiplexer_4_out), .out(subu));  // open: bin, bout
  assign bit_extender_5_out = {{16{1'b0}}, imm};  // Bit_Extender bit_extender_5
  assign bit_extender_6_out = {{16{1'b0}}, imm};  // Bit_Extender bit_extender_6
  assign bit_extender_7_out = {{16{1'b0}}, imm};  // Bit_Extender bit_extender_7
  assign bit_extender_8_out = {{16{1'b0}}, imm};  // Bit_Extender bit_extender_8
  assign \and  = I1 & multiplexer_5_out;  // AND_Gate and_1, 32 bits wide
  Multiplexer #(.width(32), .disabled(0), .enable("false")) multiplexer_5 (
    .in0(I2), .in1(bit_extender_5_out), .out(multiplexer_5_out), .sel(ALU_choose));
  assign \or  = I1 | multiplexer_6_out;  // OR_Gate or_1, 32 bits wide
  Multiplexer #(.width(32), .disabled(0), .enable("false")) multiplexer_6 (
    .in0(I2), .in1(bit_extender_6_out), .out(multiplexer_6_out), .sel(ALU_choose));
  Multiplexer #(.width(32), .disabled(0), .enable("false")) multiplexer_7 (
    .in0(I2), .in1(bit_extender_7_out), .out(multiplexer_7_out), .sel(ALU_choose));
  Multiplexer #(.width(32), .disabled(0), .enable("false")) multiplexer_8 (
    .in0(I2), .in1(bit_extender_8_out), .out(multiplexer_8_out), .sel(ALU_choose));
  assign \xor  = I1 ^ multiplexer_7_out;  // XOR_Gate xor_1, 32 bits wide
  assign \nor  = ~(I1 | multiplexer_8_out);  // NOR_Gate nor_1, 32 bits wide
  Multiplexer #(.select(5), .width(32), .disabled(0), .enable("false")) multiplexer_9 (
    .in0({32{1'b0}}), .in1(32'h1), .in15({imm, {16{1'b0}}}), .out(multiplexer_9_out), .sel(op[4:0]));  // open: in2, in3, in4, in5, in6, in7, in8, in9, in10, in11, in12, in13, in14, in16, in17, in18, in19, in20, in21, in22, in23, in24, in25, in26, in27, in28, in29, in30, in31
  Multiplexer #(.width(32), .disabled(0), .enable("false")) multiplexer_10 (
    .in0(multiplexer_9_out), .in1(multiplexer_11_out), .out(out), .sel(op[5]));
  Multiplexer #(.select(5), .width(32), .disabled(0), .enable("false")) multiplexer_11 (
    .in0(add), .in1(addu), .in2(sub), .in3(subu), .in4(\and ), .in5(\or ), .in6(\xor ), .in7(\nor ),
    .out(multiplexer_11_out), .sel(op[4:0]));  // open: in8, in9, in10, in11, in12, in13, in14, in15, in16, in17, in18, in19, in20, in21, in22, in23, in24, in25, in26, in27, in28, in29, in30, in31
  Comparator #(.width(32), .mode("unsigned")) comparator_1 (
    .a(out), .b({32{1'b0}}), .eq(comparator_1_eq));  // open: gt, lt
  or or_2 (zero, comparator_1_eq, 1'b0);

  // Other names for the same wires on the sheet: choose = ALU_choose; lui[31:16] = imm
endmodule

module DM (
  input  clk,
  input  reset,
  input  MemWrite,
  input  [15:0] A,
  input  [31:0] WD,
  output [31:0] RD
);

  wire [15:0] shifter_1_out;

  Shifter #(.width(16), .shift("lr")) shifter_1 (.in(A), .\dist (4'b0010), .out(shifter_1_out));
  RAM #(.addrWidth(16), .dataWidth(32), .bus("separate")) ram_1 (
    .addr(shifter_1_out), .din(WD), .data(RD), .str(MemWrite), .clk(clk), .ld(1'b1), .clr(reset));  // open: sel
endmodule

module Controller (
  input  [5:0] funct,
  input  [5:0] op,
  output Jump,
  output Branch,
  output RegDst,
  output RegWrite,
  output [5:0] ALUControl,
  output ALUSrc,
  output MemWrite,
  output MemtoReg
);

  wire beq, j, lui, lw, not_1_out, not_2_out, not_3_out, not_4_out, not_5_out, not_6_out, ori, R, sw;
  wire [2:0] priority_encoder_1_out;

  not not_1 (not_1_out, op[5]);
  not not_2 (not_2_out, op[4]);
  not not_3 (not_3_out, op[3]);
  not not_4 (not_4_out, op[2]);
  not not_5 (not_5_out, op[0]);
  not not_6 (not_6_out, op[1]);
  and u_R (R, not_5_out, not_6_out, not_4_out, not_3_out, not_2_out, not_1_out);
  and u_beq (beq, not_5_out, not_6_out, op[2], not_3_out, not_2_out, not_1_out);
  and u_ori (ori, op[0], not_6_out, op[2], op[3], not_2_out, not_1_out);
  and u_lw (lw, op[0], op[1], not_4_out, not_3_out, not_2_out, op[5]);
  and u_sw (sw, op[0], op[1], not_4_out, op[3], not_2_out, op[5]);
  and u_j (j, not_5_out, op[1], not_4_out, not_3_out, not_2_out, not_1_out);
  and u_lui (lui, op[0], op[1], op[2], op[3], not_2_out, not_1_out);
  Priority_Encoder #(.disabled(0)) priority_encoder_1 (
    .in0(R), .in1(beq), .in2(ori), .in3(lw), .in4(sw), .in5(j), .in6(lui), .out(priority_encoder_1_out));  // open: in7, en_in, gs, en_out
  buf u_Jump (Jump, j);  // OR_Gate
  buf u_Branch (Branch, beq);  // OR_Gate
  Multiplexer #(.select(3), .width(6), .disabled(0), .enable("false")) multiplexer_1 (
    .in0(funct), .in1(6'b100011), .in2(6'b100101), .in3(6'b100001), .in4(6'b100001), .in5(6'b000001),
    .in6(6'b001111), .out(ALUControl), .sel(priority_encoder_1_out));  // open: in7
  buf u_RegDst (RegDst, R);  // OR_Gate
  // Probe on priority_encoder_1_out
  or u_RegWrite (RegWrite, R, ori, lw, lui);
  or u_ALUSrc (ALUSrc, ori, lw, sw, lui);
  buf u_MemWrite (MemWrite, sw);  // OR_Gate
  buf u_MemtoReg (MemtoReg, lw);  // OR_Gate
endmodule
