// Logisim project P3.circ as structural Verilog: 9 circuits, main circuit main
module main (
  input  reset,
  output [31:0] out_2,
  output out_3,
  output [4:0] out_4,
  output [31:0] out_5,
  output out_6,
  output [4:0] out_7,
  output [31:0] out_8
);

  wire and_1_out, clk, controller_1_alusrc, controller_1_branch, controller_1_extop, controller_1_memtoreg,
       controller_1_regdst, eql;
  wire [2:0] controller_1_aluctr;
  wire [31:0] adder_1_out, adder_2_out, dm_1_data, ext_1_num_ex, grf_1_rd1, MemAddr, multiplexer_1_out,
       multiplexer_3_out, register_1_q, shifter_1_out;

  Multiplexer #(.width(32), .enable("false")) multiplexer_1 (
    .in0(adder_1_out), .in1(adder_2_out), .out(multiplexer_1_out), .sel(and_1_out));
  // Probe on multiplexer_1_out
  Register #(.width(32)) register_1 (.D(multiplexer_1_out), .Q(register_1_q), .clk(clk), .clr(reset));  // open: en
  and and_1 (and_1_out, controller_1_branch, eql);
  Clock clock_1 (.out(clk));
  ROM #(.addrWidth(5), .dataWidth(32)) rom_1 (.addr(register_1_q[6:2]), .data(out_2));  // open: sel
  Adder #(.width(32)) adder_1 (.a(register_1_q), .b(32'h4), .out(adder_1_out));  // open: cin, cout
  Controller controller_1 (
    .opcode(out_2[31:26]), .funct(out_2[5:0]), .RegDst(controller_1_regdst), .ALUSrc(controller_1_alusrc),
    .MemtoReg(controller_1_memtoreg), .RegWrite(out_3), .MemWrite(out_6), .Branch(controller_1_branch),
    .ExtOp(controller_1_extop), .ALUctr(controller_1_aluctr));
  // Probe on out_2[15:11]
  // Probe on out_2[15:0]
  Multiplexer #(.width(5), .enable("false")) multiplexer_2 (
    .in0(out_2[20:16]), .in1(out_2[15:11]), .out(out_4), .sel(controller_1_regdst));
  EXT ext_1 (.num(out_2[15:0]), .op(controller_1_extop), .num_ex(ext_1_num_ex));
  // Probe on ext_1_num_ex
  // Probe on grf_1_rd1
  GRF grf_1 (
    .A1(out_2[25:21]), .A2(out_2[20:16]), .WA(out_4), .WD(out_5), .RD1(grf_1_rd1), .RD2(out_8), .clk(clk),
    .reset(reset), .WE(out_3));
  Multiplexer #(.width(32), .enable("false")) multiplexer_3 (
    .in0(out_8), .in1(ext_1_num_ex), .out(multiplexer_3_out), .sel(controller_1_alusrc));
  Shifter #(.width(32)) shifter_1 (.in(ext_1_num_ex), .\dist (5'b00010), .out(shifter_1_out));
  // Probe on {MemAddr[31:7], out_7, MemAddr[1:0]}
  ALU alu_1 (
    .A(grf_1_rd1), .B(multiplexer_3_out), .Res({MemAddr[31:7], out_7, MemAddr[1:0]}), .zero(eql),
    .op(controller_1_aluctr));
  // Probe on shifter_1_out
  DM dm_1 (
    .DA({MemAddr[31:7], out_7, MemAddr[1:0]}), .DM(out_8), .clk(clk), .MR(1'b1), .MW(out_6), .reset(reset),
    .Data(dm_1_data));
  // Probe on out_2[15:0]
  Adder #(.width(32)) adder_2 (.a(shifter_1_out), .b(adder_1_out), .out(adder_2_out));  // open: cin, cout
  // Probe on adder_2_out
  Multiplexer #(.width(32), .enable("false")) multiplexer_4 (
    .in0({MemAddr[31:7], out_7, MemAddr[1:0]}), .in1(dm_1_data), .out(out_5), .sel(controller_1_memtoreg));

  // Other names for the same wires on the sheet: func[5:0] = out_2[5:0]; imme[15:0] = out_2[15:0];
  //   Instr[31:0] = out_2; MemAddr[6:2] = out_7; MemData[31:0] = out_8; MemWrite = out_6; Opcode[5:0] = out_2[31:26];
  //   RA1[4:0] = out_2[25:21]; RA2[4:0] = out_2[20:16]; RA3[4:0] = out_2[15:11]; RegWrite = out_3;
  //   RegAddr[4:0] = out_4; WA[4:0] = out_4; RegData[31:0] = out_5; WD[31:0] = out_5

  // Notes on the sheet:
  //   contents of rom_1 (hex, n*v repeats v):
  //   341c0000 341d0000 34013456 210820 8c010004 ac010004 3c027878 411822 3c051234 34040005 0 ac85ffff
  //   8c83ffff 10650001 1000000d 34670404 10e3000b 0 3c087777 3508ffff 80022 34001100 e65020 34080000
  //   34090001 340a0001 10a4020 1109fffe 1000ffff
endmodule

module EXT (
  input  [15:0] num,
  input  op,
  output [31:0] num_ex
);

  wire [31:0] bit_extender_1_out, bit_extender_2_out;

  assign bit_extender_1_out = {{16{1'b0}}, num};  // Bit_Extender bit_extender_1
  assign bit_extender_2_out = {{16{num[15]}}, num};  // Bit_Extender bit_extender_2
  Multiplexer #(.width(32), .enable("false")) multiplexer_1 (
    .in0(bit_extender_1_out), .in1(bit_extender_2_out), .out(num_ex), .sel(op));
endmodule

module GRF (
  input  clk,
  input  reset,
  input  WE,
  input  [4:0] A1,
  input  [4:0] A2,
  input  [4:0] WA,
  input  [31:0] WD,
  output [31:0] RD1,
  output [31:0] RD2
);

  wire in0, in1, in2, in3, in4, in5, in6, in7, in8, in9, in10, in11, in12, in13, in14, in15, in16, in17,
       in18, in19, in20, in21, in22, in23, in24, in25, in26, in27, in28, in29, in30, in31;
  wire [31:0] multiplexer_1_out, multiplexer_2_out, multiplexer_3_out, multiplexer_4_out, multiplexer_5_out,
       multiplexer_6_out, multiplexer_7_out, multiplexer_8_out, multiplexer_9_out, multiplexer_10_out,
       multiplexer_11_out, multiplexer_12_out, multiplexer_13_out, multiplexer_14_out, multiplexer_15_out,
       multiplexer_16_out, multiplexer_17_out, multiplexer_18_out, multiplexer_19_out, multiplexer_20_out,
       multiplexer_21_out, multiplexer_22_out, multiplexer_23_out, multiplexer_24_out, multiplexer_25_out,
       multiplexer_26_out, multiplexer_27_out, multiplexer_28_out, multiplexer_29_out, multiplexer_30_out,
       multiplexer_31_out, out1, out2, out3, out4, out5, out6, out7, out8, out9, out10, out11, out12, out13,
       out14, out15, out16, out17, out18, out19, out20, out21, out22, out23, out24, out25, out26, out27,
       out28, out29, out30, out31;

  Demultiplexer #(.select(5)) demultiplexer_1 (
    .out0(in0), .out1(in1), .out2(in2), .out3(in3), .out4(in4), .out5(in5), .out6(in6), .out7(in7),
    .out8(in8), .out9(in9), .out10(in10), .out11(in11), .out12(in12), .out13(in13), .out14(in14),
    .out15(in15), .out16(in16), .out17(in17), .out18(in18), .out19(in19), .out20(in20), .out21(in21),
    .out22(in22), .out23(in23), .out24(in24), .out25(in25), .out26(in26), .out27(in27), .out28(in28),
    .out29(in29), .out30(in30), .out31(in31), .in(1'b1), .sel(WA), .en(WE));
  Multiplexer #(.width(32), .enable("false")) multiplexer_1 (.in0(out1), .in1(WD), .out(multiplexer_1_out), .sel(in1));
  Multiplexer #(.width(32), .enable("false")) multiplexer_2 (.in0(out2), .in1(WD), .out(multiplexer_2_out), .sel(in2));
  Multiplexer #(.width(32), .enable("false")) multiplexer_3 (.in0(out3), .in1(WD), .out(multiplexer_3_out), .sel(in3));
  Multiplexer #(.width(32), .enable("false")) multiplexer_4 (.in0(out4), .in1(WD), .out(multiplexer_4_out), .sel(in4));
  Multiplexer #(.width(32), .enable("false")) multiplexer_5 (.in0(out5), .in1(WD), .out(multiplexer_5_out), .sel(in5));
  Multiplexer #(.width(32), .enable("false")) multiplexer_6 (.in0(out6), .in1(WD), .out(multiplexer_6_out), .sel(in6));
  Multiplexer #(.width(32), .enable("false")) multiplexer_7 (.in0(out7), .in1(WD), .out(multiplexer_7_out), .sel(in7));
  Multiplexer #(.width(32), .enable("false")) multiplexer_8 (.in0(out8), .in1(WD), .out(multiplexer_8_out), .sel(in8));
  Multiplexer #(.width(32), .enable("false")) multiplexer_9 (.in0(out9), .in1(WD), .out(multiplexer_9_out), .sel(in9));
  Multiplexer #(.width(32), .enable("false")) multiplexer_10 (
    .in0(out10), .in1(WD), .out(multiplexer_10_out), .sel(in10));
  Multiplexer #(.width(32), .enable("false")) multiplexer_11 (
    .in0(out11), .in1(WD), .out(multiplexer_11_out), .sel(in11));
  Multiplexer #(.width(32), .enable("false")) multiplexer_12 (
    .in0(out12), .in1(WD), .out(multiplexer_12_out), .sel(in12));
  Multiplexer #(.width(32), .enable("false")) multiplexer_13 (
    .in0(out13), .in1(WD), .out(multiplexer_13_out), .sel(in13));
  Multiplexer #(.width(32), .enable("false")) multiplexer_14 (
    .in0(out14), .in1(WD), .out(multiplexer_14_out), .sel(in14));
  Multiplexer #(.width(32), .enable("false")) multiplexer_15 (
    .in0(out15), .in1(WD), .out(multiplexer_15_out), .sel(in15));
  Register #(.width(32)) register_1 (.D(multiplexer_1_out), .Q(out1), .clk(clk), .clr(reset));  // open: en
  Register #(.width(32)) register_2 (.D(multiplexer_2_out), .Q(out2), .clk(clk), .clr(reset));  // open: en
  Register #(.width(32)) register_3 (.D(multiplexer_3_out), .Q(out3), .clk(clk), .clr(reset));  // open: en
  Register #(.width(32)) register_4 (.D(multiplexer_4_out), .Q(out4), .clk(clk), .clr(reset));  // open: en
  Register #(.width(32)) register_5 (.D(multiplexer_5_out), .Q(out5), .clk(clk), .clr(reset));  // open: en
  Register #(.width(32)) register_6 (.D(multiplexer_6_out), .Q(out6), .clk(clk), .clr(reset));  // open: en
  Register #(.width(32)) register_7 (.D(multiplexer_7_out), .Q(out7), .clk(clk), .clr(reset));  // open: en
  Register #(.width(32)) register_8 (.D(multiplexer_8_out), .Q(out8), .clk(clk), .clr(reset));  // open: en
  Register #(.width(32)) register_9 (.D(multiplexer_9_out), .Q(out9), .clk(clk), .clr(reset));  // open: en
  Register #(.width(32)) register_10 (.D(multiplexer_10_out), .Q(out10), .clk(clk), .clr(reset));  // open: en
  Register #(.width(32)) register_11 (.D(multiplexer_11_out), .Q(out11), .clk(clk), .clr(reset));  // open: en
  Register #(.width(32)) register_12 (.D(multiplexer_12_out), .Q(out12), .clk(clk), .clr(reset));  // open: en
  Register #(.width(32)) register_13 (.D(multiplexer_13_out), .Q(out13), .clk(clk), .clr(reset));  // open: en
  Register #(.width(32)) register_14 (.D(multiplexer_14_out), .Q(out14), .clk(clk), .clr(reset));  // open: en
  Register #(.width(32)) register_15 (.D(multiplexer_15_out), .Q(out15), .clk(clk), .clr(reset));  // open: en
  Multiplexer #(.width(32), .enable("false")) multiplexer_16 (
    .in0(out16), .in1(WD), .out(multiplexer_16_out), .sel(in16));
  Multiplexer #(.width(32), .enable("false")) multiplexer_17 (
    .in0(out17), .in1(WD), .out(multiplexer_17_out), .sel(in17));
  Multiplexer #(.width(32), .enable("false")) multiplexer_18 (
    .in0(out18), .in1(WD), .out(multiplexer_18_out), .sel(in18));
  Multiplexer #(.width(32), .enable("false")) multiplexer_19 (
    .in0(out19), .in1(WD), .out(multiplexer_19_out), .sel(in19));
  Multiplexer #(.width(32), .enable("false")) multiplexer_20 (
    .in0(out20), .in1(WD), .out(multiplexer_20_out), .sel(in20));
  Multiplexer #(.width(32), .enable("false")) multiplexer_21 (
    .in0(out21), .in1(WD), .out(multiplexer_21_out), .sel(in21));
  Multiplexer #(.width(32), .enable("false")) multiplexer_22 (
    .in0(out22), .in1(WD), .out(multiplexer_22_out), .sel(in22));
  Multiplexer #(.width(32), .enable("false")) multiplexer_23 (
    .in0(out23), .in1(WD), .out(multiplexer_23_out), .sel(in23));
  Multiplexer #(.width(32), .enable("false")) multiplexer_24 (
    .in0(out24), .in1(WD), .out(multiplexer_24_out), .sel(in24));
  Multiplexer #(.width(32), .enable("false")) multiplexer_25 (
    .in0(out25), .in1(WD), .out(multiplexer_25_out), .sel(in25));
  Multiplexer #(.width(32), .enable("false")) multiplexer_26 (
    .in0(out26), .in1(WD), .out(multiplexer_26_out), .sel(in26));
  Multiplexer #(.width(32), .enable("false")) multiplexer_27 (
    .in0(out27), .in1(WD), .out(multiplexer_27_out), .sel(in27));
  Multiplexer #(.width(32), .enable("false")) multiplexer_28 (
    .in0(out28), .in1(WD), .out(multiplexer_28_out), .sel(in28));
  Multiplexer #(.width(32), .enable("false")) multiplexer_29 (
    .in0(out29), .in1(WD), .out(multiplexer_29_out), .sel(in29));
  Multiplexer #(.width(32), .enable("false")) multiplexer_30 (
    .in0(out30), .in1(WD), .out(multiplexer_30_out), .sel(in30));
  Multiplexer #(.width(32), .enable("false")) multiplexer_31 (
    .in0(out31), .in1(WD), .out(multiplexer_31_out), .sel(in31));
  Register #(.width(32)) register_16 (.D(multiplexer_16_out), .Q(out16), .clk(clk), .clr(reset));  // open: en
  Register #(.width(32)) register_17 (.D(multiplexer_17_out), .Q(out17), .clk(clk), .clr(reset));  // open: en
  Register #(.width(32)) register_18 (.D(multiplexer_18_out), .Q(out18), .clk(clk), .clr(reset));  // open: en
  Register #(.width(32)) register_19 (.D(multiplexer_19_out), .Q(out19), .clk(clk), .clr(reset));  // open: en
  Register #(.width(32)) register_20 (.D(multiplexer_20_out), .Q(out20), .clk(clk), .clr(reset));  // open: en
  Register #(.width(32)) register_21 (.D(multiplexer_21_out), .Q(out21), .clk(clk), .clr(reset));  // open: en
  Register #(.width(32)) register_22 (.D(multiplexer_22_out), .Q(out22), .clk(clk), .clr(reset));  // open: en
  Register #(.width(32)) register_23 (.D(multiplexer_23_out), .Q(out23), .clk(clk), .clr(reset));  // open: en
  Register #(.width(32)) register_24 (.D(multiplexer_24_out), .Q(out24), .clk(clk), .clr(reset));  // open: en
  Register #(.width(32)) register_25 (.D(multiplexer_25_out), .Q(out25), .clk(clk), .clr(reset));  // open: en
  Register #(.width(32)) register_26 (.D(multiplexer_26_out), .Q(out26), .clk(clk), .clr(reset));  // open: en
  Register #(.width(32)) register_27 (.D(multiplexer_27_out), .Q(out27), .clk(clk), .clr(reset));  // open: en
  Register #(.width(32)) register_28 (.D(multiplexer_28_out), .Q(out28), .clk(clk), .clr(reset));  // open: en
  Register #(.width(32)) register_29 (.D(multiplexer_29_out), .Q(out29), .clk(clk), .clr(reset));  // open: en
  Register #(.width(32)) register_30 (.D(multiplexer_30_out), .Q(out30), .clk(clk), .clr(reset));  // open: en
  Register #(.width(32)) register_31 (.D(multiplexer_31_out), .Q(out31), .clk(clk), .clr(reset));  // open: en
  Multiplexer #(.select(5), .width(32), .enable("false")) multiplexer_32 (
    .in0({32{1'b0}}), .in1(out1), .in2(out2), .in3(out3), .in4(out4), .in5(out5), .in6(out6), .in7(out7),
    .in8(out8), .in9(out9), .in10(out10), .in11(out11), .in12(out12), .in13(out13), .in14(out14),
    .in15(out15), .in16(out16), .in17(out17), .in18(out18), .in19(out19), .in20(out20), .in21(out21),
    .in22(out22), .in23(out23), .in24(out24), .in25(out25), .in26(out26), .in27(out27), .in28(out28),
    .in29(out29), .in30(out30), .in31(out31), .out(RD1), .sel(A1));
  Multiplexer #(.select(5), .width(32), .enable("false")) multiplexer_33 (
    .in0({32{1'b0}}), .in1(out1), .in2(out2), .in3(out3), .in4(out4), .in5(out5), .in6(out6), .in7(out7),
    .in8(out8), .in9(out9), .in10(out10), .in11(out11), .in12(out12), .in13(out13), .in14(out14),
    .in15(out15), .in16(out16), .in17(out17), .in18(out18), .in19(out19), .in20(out20), .in21(out21),
    .in22(out22), .in23(out23), .in24(out24), .in25(out25), .in26(out26), .in27(out27), .in28(out28),
    .in29(out29), .in30(out30), .in31(out31), .out(RD2), .sel(A2));

  // Other names for the same wires on the sheet: write = WE
endmodule

module ALU (
  input  [2:0] op,
  input  [31:0] A,
  input  [31:0] B,
  output [31:0] Res,
  output zero
);

  wire comparator_1_lt;
  wire [31:0] add, \and , lui, \or , slt, sub;

  Adder #(.width(32)) adder_1 (.a(A), .b(B), .out(add));  // open: cin, cout
  assign \or  = A | B;  // OR_Gate or_1, 32 bits wide
  assign \and  = A & B;  // AND_Gate and_1, 32 bits wide
  Subtractor #(.width(32)) subtractor_1 (.a(A), .b(B), .out(sub));  // open: bin, bout
  Comparator #(.width(32), .mode("unsigned")) comparator_1 (.a(A), .b(B), .lt(comparator_1_lt));  // open: gt, eq
  Shifter #(.width(32)) shifter_1 (.in(B), .\dist (5'b10000), .out(lui));
  assign slt = {{31{1'b0}}, comparator_1_lt};  // Bit_Extender bit_extender_1
  Comparator #(.width(32), .mode("unsigned")) comparator_2 (.a(sub), .b({32{1'b0}}), .eq(zero));  // open: gt, lt
  Multiplexer #(.select(3), .width(32), .enable("false")) multiplexer_1 (
    .in0(add), .in1(sub), .in2(\and ), .in3(\or ), .in4(lui), .in7(slt), .out(Res), .sel(op));  // open: in5, in6
endmodule

module Controller (
  input  [5:0] opcode,
  input  [5:0] funct,
  output RegDst,
  output ALUSrc,
  output MemtoReg,
  output RegWrite,
  output MemWrite,
  output Branch,
  output ExtOp,
  output [2:0] ALUctr
);

  wire mde_1_aluop0, mde_1_aluop1, mde_1_aluop2;

  MDE mde_1 (
    .opcode(opcode), .ALUOp2(mde_1_aluop2), .ALUOp1(mde_1_aluop1), .ALUOp0(mde_1_aluop0), .RegDst(RegDst),
    .ALUSrc(ALUSrc), .MemtoReg(MemtoReg), .RegWrite(RegWrite), .MemWrite(MemWrite), .Branch(Branch),
    .ExtOp(ExtOp));
  ALUDE alude_1 (.Func(funct), .ALUOp2(mde_1_aluop2), .ALUOp1(mde_1_aluop1), .ALUOp0(mde_1_aluop0), .ALUctr(ALUctr));
endmodule

module MDE (
  input  [5:0] opcode,
  output RegDst,
  output ALUSrc,
  output MemtoReg,
  output RegWrite,
  output MemWrite,
  output Branch,
  output ExtOp,
  output ALUOp2,
  output ALUOp1,
  output ALUOp0
);

  wire add_sub, beq, lui, lw, not_1_out, not_2_out, not_3_out, not_4_out, not_5_out, not_6_out, ori, sw;

  not not_1 (not_1_out, opcode[5]);
  not not_2 (not_2_out, opcode[4]);
  not not_3 (not_3_out, opcode[3]);
  not not_4 (not_4_out, opcode[1]);
  not not_5 (not_5_out, opcode[2]);
  not not_6 (not_6_out, opcode[0]);
  and u_add_sub (add_sub, not_1_out, not_2_out, not_3_out, not_5_out, not_4_out, not_6_out);
  and u_ori (ori, not_1_out, not_2_out, opcode[3], opcode[2], not_4_out, opcode[0]);
  and u_lw (lw, opcode[5], not_2_out, not_3_out, not_5_out, opcode[1], opcode[0]);
  and u_sw (sw, opcode[5], not_2_out, opcode[3], not_5_out, opcode[1], opcode[0]);
  and u_beq (beq, not_1_out, not_2_out, not_3_out, opcode[2], not_4_out, not_6_out);
  and u_lui (lui, not_1_out, not_2_out, opcode[3], opcode[2], opcode[1], opcode[0]);
  buf or_1 (RegDst, add_sub);  // OR_Gate
  or or_2 (ALUSrc, ori, lw, sw, lui);
  buf or_3 (MemtoReg, lw);  // OR_Gate
  or or_4 (RegWrite, add_sub, ori, lw, lui);
  buf or_5 (MemWrite, sw);  // OR_Gate
  buf or_6 (Branch, beq);  // OR_Gate
  or or_7 (ExtOp, lw, sw, beq);
  or or_8 (ALUOp2, add_sub, lui);
  or or_9 (ALUOp1, ori, add_sub, 1'b0);
  or or_10 (ALUOp0, ori, add_sub, 1'b0);

  // Other names for the same wires on the sheet: op0 = opcode[0]; op1 = opcode[1]; op2 = opcode[2]; op3 = opcode[3];
  //   op4 = opcode[4]; op5 = opcode[5]
endmodule

module ALUDE (
  input  ALUOp2,
  input  ALUOp1,
  input  ALUOp0,
  input  [5:0] Func,
  output [2:0] ALUctr
);

  wire add_out, and_out, not_1_out, not_2_out, not_3_out, not_4_out, not_5_out, not_6_out, or_out, sub_out;
  wire [2:0] alude_fun_1_ctr0;

  not not_1 (not_1_out, Func[4]);
  not not_2 (not_2_out, Func[5]);
  not not_3 (not_3_out, Func[3]);
  not not_4 (not_4_out, Func[2]);
  not not_5 (not_5_out, Func[1]);
  not not_6 (not_6_out, Func[0]);
  and add (add_out, Func[5], not_1_out, not_3_out, not_4_out, not_5_out, not_6_out);
  and sub (sub_out, Func[5], not_1_out, not_3_out, not_4_out, Func[1], not_6_out);
  and \and  (and_out, Func[5], not_1_out, not_3_out, Func[2], not_5_out, not_6_out);
  and \or  (or_out, Func[5], not_1_out, not_3_out, Func[2], not_5_out, Func[0]);
  ALUDE_fun alude_fun_1 (
    .add(add_out), .sub(sub_out), .\and (and_out), .\or (or_out), .ctr2(alude_fun_1_ctr0[2]),
    .ctr1(alude_fun_1_ctr0[1]), .ctr0(alude_fun_1_ctr0[0]));
  Multiplexer #(.select(3), .width(3), .enable("false")) multiplexer_1 (
    .in0(3'b000), .in1(3'b001), .in2(3'b010), .in3(3'b011), .in4(3'b100), .in5(alude_fun_1_ctr0),
    .in6(alude_fun_1_ctr0), .in7(alude_fun_1_ctr0), .out(ALUctr), .sel({ALUOp2, ALUOp1, ALUOp0}));

  // Other names for the same wires on the sheet: op0 = Func[0]; op1 = Func[1]; op2 = Func[2]; op3 = Func[3];
  //   op4 = Func[4]; op5 = Func[5]
endmodule

module DM (
  input  clk,
  input  MR,
  input  MW,
  input  reset,
  input  [31:0] DA,
  input  [31:0] DM,
  output [31:0] Data
);

  RAM #(.addrWidth(5), .dataWidth(32), .bus("separate")) ram_1 (
    .addr(DA[6:2]), .din(DM), .data(Data), .str(MW), .clk(clk), .ld(MR), .clr(reset));  // open: sel
endmodule

module ALUDE_fun (
  input  add,
  input  sub,
  input  \and ,
  input  \or ,
  output ctr2,
  output ctr1,
  output ctr0
);

  wire not_1_out, not_2_out, not_3_out, not_4_out;

  not not_1 (not_1_out, add);
  and and_1 (ctr1, not_1_out, not_2_out);
  not not_2 (not_2_out, sub);
  not not_3 (not_3_out, add);
  and and_2 (ctr0, not_3_out, not_4_out);
  not not_4 (not_4_out, \and );

  assign ctr2 = 1'b0;
endmodule
